# Fritzing sketch Robot schematic (saved by Fritzing 0.9.2b)
breadboards: 1

parts:
  Arduino = Arduino Leonardo (Rev3b)
  H-bridge = H-Bridge [package=THT]
  battery = DC Power [voltage=12V]
  MLEFT = DC Motor
  MRIGHT = DC Motor
  Motor_Shield = Rotoshield - Motor driver shield for Arduino
  battery2 = DC Power [voltage=6]
  Claw_1 = DC Motor
  Claw_2 = DC Motor
  Claw_3 = DC Motor
  Claw_4 = DC Motor
  Wireless_PS2_Transmitter = male pin header, 6 pins [form="♂ (male)"]

nets:
  N1: Arduino.D6_PWM/A7, H-bridge.1A
  N2: Arduino.D7, H-bridge.2A
  N3: Arduino.3V3, Wireless_PS2_Transmitter.pin4
  GND: Arduino.GND, H-bridge.GND1, H-bridge.GND2, H-bridge.GND3, H-bridge.GND4, battery.V-, Wireless_PS2_Transmitter.pin3
  N4: Arduino.VIN, H-bridge.1_2EN, H-bridge.VCC2, H-bridge.3_4EN, H-bridge.VCC1, battery.V+
  N5: Arduino.D8/A8, H-bridge.3A
  N6: Arduino.D9_PWM/A9, H-bridge.4A
  N7: Arduino.D10_PWM/A10, Wireless_PS2_Transmitter.pin5
  N8: Arduino.D11_PWM, Wireless_PS2_Transmitter.pin2
  N9: Arduino.D12/A11, Wireless_PS2_Transmitter.pin1
  N10: Arduino.D13_PWM, Wireless_PS2_Transmitter.pin6
  N11: H-bridge.1Y, MRIGHT.pin_2
  N12: H-bridge.2Y, MRIGHT.pin_1
  N13: H-bridge.3Y, MLEFT.pin_2
  N14: H-bridge.4Y, MLEFT.pin_1
  N15: Motor_Shield.GND, battery2.V-
  N16: Motor_Shield.M1-2, Claw_1.pin_2
  N17: Motor_Shield.M1-1, Claw_1.pin_1
  N18: Motor_Shield.M2-2, Claw_2.pin_2
  N19: Motor_Shield.M2-1, Claw_2.pin_1
  N20: Motor_Shield.M3-2, Claw_3.pin_2
  N21: Motor_Shield.M3-1, Claw_3.pin_1
  N22: Motor_Shield.M4-2, Claw_4.pin_2
  N23: Motor_Shield.M4-1, Claw_4.pin_1
  N24: Motor_Shield.VCC, battery2.V+
